// Digital circuit 16_bit_alu.dig as structural Verilog
module _16_bit_alu (
  input  AR3,
  input  AR2,
  input  AR1,
  input  AR0,
  input  AL,
  input  A15,
  input  A14,
  input  A13,
  input  A12,
  input  A11,
  input  A10,
  input  A9,
  input  A8,
  input  A7,
  input  A6,
  input  A5,
  input  A4,
  input  A3,
  input  A2,
  input  A1,
  input  A0,
  input  B15,
  input  B14,
  input  B13,
  input  B12,
  input  B11,
  input  B10,
  input  B9,
  input  B8,
  input  B7,
  input  B6,
  input  B5,
  input  B4,
  input  B3,
  input  B2,
  input  B1,
  input  B0,
  input  CLK,
  output Q15,
  output Q14,
  output Q13,
  output Q12,
  output Q11,
  output Q10,
  output Q9,
  output Q8,
  output Q7,
  output Q6,
  output Q5,
  output Q4,
  output Q3,
  output Q2,
  output Q1,
  output Q0,
  output C15
);

  wire alu_slice_1_2_co, alu_slice_1_3_co, alu_slice_1_4_co;

  LED led_1 (.in(C15));
  alu_slice_1 alu_slice_1_1 (
    .Ci(alu_slice_1_2_co), .AL(AL), .AR0(AR0), .AR1(AR1), .AR2(AR2), .AR3(AR3), .ALU0(A12), .ALU1(A13),
    .ALU2(A14), .ALU3(A15), .BUS0(B12), .BUS1(B13), .BUS2(B14), .BUS3(B15), .CLK(CLK), .Co(C15), .AC0(Q12),
    .AC1(Q13), .AC2(Q14), .AC3(Q15));
  alu_slice_1 alu_slice_1_2 (
    .Ci(alu_slice_1_3_co), .AL(AL), .AR0(AR0), .AR1(AR1), .AR2(AR2), .AR3(AR3), .ALU0(A8), .ALU1(A9),
    .ALU2(A10), .ALU3(A11), .BUS0(B8), .BUS1(B9), .BUS2(B10), .BUS3(B11), .CLK(CLK), .Co(alu_slice_1_2_co),
    .AC0(Q8), .AC1(Q9), .AC2(Q10), .AC3(Q11));
  alu_slice_1 alu_slice_1_3 (
    .Ci(alu_slice_1_4_co), .AL(AL), .AR0(AR0), .AR1(AR1), .AR2(AR2), .AR3(AR3), .ALU0(A4), .ALU1(A5),
    .ALU2(A6), .ALU3(A7), .BUS0(B4), .BUS1(B5), .BUS2(B6), .BUS3(B7), .CLK(CLK), .Co(alu_slice_1_3_co),
    .AC0(Q4), .AC1(Q5), .AC2(Q6), .AC3(Q7));
  alu_slice_1 alu_slice_1_4 (
    .Ci(AR0), .AL(AL), .AR0(AR0), .AR1(AR1), .AR2(AR2), .AR3(AR3), .ALU0(A0), .ALU1(A1), .ALU2(A2),
    .ALU3(A3), .BUS0(B0), .BUS1(B1), .BUS2(B2), .BUS3(B3), .CLK(CLK), .Co(alu_slice_1_4_co), .AC0(Q0),
    .AC1(Q1), .AC2(Q2), .AC3(Q3));
  LED led_2 (.in(Q15));
  LED led_3 (.in(Q14));
  LED led_4 (.in(Q13));
  LED led_5 (.in(Q12));
  LED led_6 (.in(Q11));
  LED led_7 (.in(Q10));
  LED led_8 (.in(Q9));
  LED led_9 (.in(Q8));
  LED led_10 (.in(Q7));
  LED led_11 (.in(Q6));
  LED led_12 (.in(Q5));
  LED led_13 (.in(Q4));
  LED led_14 (.in(Q3));
  LED led_15 (.in(Q2));
  LED led_16 (.in(Q1));
  LED led_17 (.in(Q0));
endmodule
