// Digital circuit 4_bit_cpu_1.dig as structural Verilog
module _4_bit_cpu_1 (
  input  BUS7,
  input  BUS6,
  input  BUS5,
  input  BUS4,
  input  CLK1
);

  wire _28c16_1_p9, _28c16_1_p10, _28c16_1_p11, _28c16_1_p20, _28c16_1_p21, _28c16_1_p22, _7425_1_pin8,
       _74138_1_pin1, _74138_1_pin2, _74138_1_pin3, _74138_1_pin7, _74138_1_pin9, _74138_1_pin10,
       _74138_1_pin11, _74138_1_pin12, _74138_1_pin13, _74138_1_pin14, _74138_1_pin15, _74153_1_pin1,
       _74161_1_pin1, _74161_1_pin10, _74161_1_pin11, _74161_1_pin12, _74161_1_pin13, _74161_1_pin14,
       _74161_2_pin3, _74161_2_pin4, _74161_2_pin5, _74161_2_pin6, _74161_2_pin11, _74161_2_pin12,
       _74161_2_pin13, _74161_2_pin14, _74173_1_pin3, _74173_1_pin14, _74173_2_pin3, _74173_2_pin4,
       _74173_2_pin5, _74173_2_pin6, _74173_2_pin11, _74244_1_pin12, _74244_1_pin14, _74244_1_pin16,
       _74244_1_pin18, _74541_1_pin1, _74541_1_pin11, _74541_1_pin12, _74541_1_pin13, _74541_1_pin14,
       _74541_1_pin15, _74541_1_pin16, _74541_1_pin17, _74541_1_pin18, _74541_2_pin6, _74541_2_pin7,
       _74541_2_pin8, _74541_2_pin9, _74541_3_pin1, alu_slice_1_1_co, diodebackward_1_out,
       diodebackward_3_out, diodebackward_7_out, diodebackward_12_out, diodebackward_15_out, not_1_out,
       not_2_out, not_3_out, not_4_out, not_5_out, not_6_out, not_8_out, not_10_out, or_1_out;

  LED led_1 (.in(_74138_1_pin3));
  LED led_2 (.in(_74138_1_pin2));
  LED led_3 (.in(_74138_1_pin1));
  LED led_4 (.in(_74173_1_pin3));
  _74138 _74138_1 (
    .pin1(_74138_1_pin1), .pin2(_74138_1_pin2), .pin3(_74138_1_pin3), .pin4(1'b0), .pin5(1'b0), .pin6(1'b1),
    .pin7(_74138_1_pin7), .pin8(1'b0), .pin9(_74138_1_pin9), .pin10(_74138_1_pin10), .pin11(_74138_1_pin11),
    .pin12(_74138_1_pin12), .pin13(_74138_1_pin13), .pin14(_74138_1_pin14), .pin15(_74138_1_pin15),
    .pin16(1'b1));
  DiodeBackward diodebackward_1 (.in(_74138_1_pin3), .out(diodebackward_1_out));
  DiodeBackward diodebackward_2 (.in(_74138_1_pin7), .out(diodebackward_1_out));
  PullUp pullup_1 (.out(diodebackward_1_out));
  DiodeBackward diodebackward_3 (.in(_74138_1_pin15), .out(diodebackward_3_out));
  DiodeBackward diodebackward_4 (.in(_74138_1_pin14), .out(diodebackward_3_out));
  DiodeBackward diodebackward_5 (.in(_74138_1_pin13), .out(diodebackward_3_out));
  DiodeBackward diodebackward_6 (.in(_74138_1_pin11), .out(diodebackward_3_out));
  not not_1 (not_1_out, diodebackward_1_out);
  LED led_5 (.in(not_1_out));
  PullUp pullup_2 (.out(diodebackward_3_out));
  DiodeBackward diodebackward_7 (.in(_74138_1_pin15), .out(diodebackward_7_out));
  DiodeBackward diodebackward_8 (.in(_74138_1_pin13), .out(diodebackward_7_out));
  DiodeBackward diodebackward_9 (.in(_74138_1_pin12), .out(diodebackward_7_out));
  DiodeBackward diodebackward_10 (.in(_74138_1_pin11), .out(diodebackward_7_out));
  DiodeBackward diodebackward_11 (.in(_74138_1_pin7), .out(diodebackward_7_out));
  not not_2 (not_2_out, diodebackward_3_out);
  LED led_6 (.in(not_2_out));
  PullUp pullup_3 (.out(diodebackward_7_out));
  DiodeBackward diodebackward_12 (.in(_74138_1_pin13), .out(diodebackward_12_out));
  DiodeBackward diodebackward_13 (.in(_74138_1_pin12), .out(diodebackward_12_out));
  DiodeBackward diodebackward_14 (.in(_74138_1_pin10), .out(diodebackward_12_out));
  not not_3 (not_3_out, diodebackward_7_out);
  LED led_7 (.in(not_3_out));
  PullUp pullup_4 (.out(diodebackward_12_out));
  DiodeBackward diodebackward_15 (.in(_74138_1_pin10), .out(diodebackward_15_out));
  DiodeBackward diodebackward_16 (.in(_74138_1_pin7), .out(diodebackward_15_out));
  not not_4 (not_4_out, diodebackward_12_out);
  LED led_8 (.in(not_4_out));
  PullUp pullup_5 (.out(diodebackward_15_out));
  not not_5 (not_5_out, diodebackward_15_out);
  LED led_9 (.in(not_5_out));
  not not_6 (not_6_out, CLK1);
  _74161 _74161_1 (
    .pin1(_74161_1_pin1), .pin2(CLK1), .pin3(BUS4), .pin4(BUS5), .pin5(BUS6), .pin6(BUS7), .pin7(1'b1),
    .pin8(1'b0), .pin9(1'b1), .pin10(_74161_1_pin10), .pin11(_74161_1_pin11), .pin12(_74161_1_pin12),
    .pin13(_74161_1_pin13), .pin14(_74161_1_pin14), .pin16(1'b1));  // open: pin15
  _74161 _74161_2 (
    .pin1(_74161_1_pin1), .pin2(CLK1), .pin3(_74161_2_pin3), .pin4(_74161_2_pin4), .pin5(_74161_2_pin5),
    .pin6(_74161_2_pin6), .pin7(1'b1), .pin8(1'b0), .pin9(1'b1), .pin10(1'b1), .pin11(_74161_2_pin11),
    .pin12(_74161_2_pin12), .pin13(_74161_2_pin13), .pin14(_74161_2_pin14), .pin15(_74161_1_pin10),
    .pin16(1'b1));
  LED led_10 (.in(_74161_1_pin11));
  LED led_11 (.in(_74161_1_pin12));
  LED led_12 (.in(_74161_1_pin13));
  LED led_13 (.in(_74161_2_pin11));
  LED led_14 (.in(_74161_1_pin14));
  LED led_15 (.in(_74161_2_pin12));
  LED led_16 (.in(_74161_2_pin13));
  LED led_17 (.in(_74161_2_pin14));
  // _28c16 _28c16_1: pin names not known; wires that end beside it: _74161_1_pin11, _74161_1_pin12, _74161_1_pin13, _74161_1_pin14, _74161_2_pin11, _74161_2_pin12, _74161_2_pin13, _74161_2_pin14, _28c16_1_p9, _28c16_1_p10, _28c16_1_p11, 1'b0, 1'b1, 1'b0, 1'b0, 1'b1, 1'b0, 1'b0, 1'b0, _28c16_1_p20, _28c16_1_p21, _28c16_1_p22
  _74541 _74541_1 (
    .pin1(_74541_1_pin1), .pin2(_74161_1_pin11), .pin3(_74161_1_pin12), .pin4(_74161_1_pin13),
    .pin5(_74161_1_pin14), .pin6(_74161_2_pin11), .pin7(_74161_2_pin12), .pin8(_74161_2_pin13),
    .pin9(_74161_2_pin14), .pin10(1'b0), .pin11(_74541_1_pin11), .pin12(_74541_1_pin12),
    .pin13(_74541_1_pin13), .pin14(_74541_1_pin14), .pin15(_74541_1_pin15), .pin16(_74541_1_pin16),
    .pin17(_74541_1_pin17), .pin18(_74541_1_pin18), .pin19(_74541_1_pin1), .pin20(1'b1));
  _74541 _74541_2 (
    .pin1(_74138_1_pin9), .pin2(1'b0), .pin3(1'b0), .pin4(1'b0), .pin5(1'b0), .pin6(_74541_2_pin6),
    .pin7(_74541_2_pin7), .pin8(_74541_2_pin8), .pin9(_74541_2_pin9), .pin10(1'b0), .pin11(_74161_2_pin3),
    .pin12(_74161_2_pin4), .pin13(_74161_2_pin5), .pin14(_74161_2_pin6), .pin19(_74138_1_pin9), .pin20(1'b1));  // open: pin15, pin16, pin17, pin18
  LED led_18 (.in(_74541_1_pin18));
  LED led_19 (.in(_74541_1_pin17));
  LED led_20 (.in(_74541_1_pin16));
  alu_slice_1 alu_slice_1_1 (
    .Ci(not_5_out), .AL(not_1_out), .AR0(not_5_out), .AR1(not_4_out), .AR2(not_3_out), .AR3(not_2_out),
    .ALU0(_74541_2_pin9), .ALU1(_74541_2_pin8), .ALU2(_74541_2_pin7), .ALU3(_74541_2_pin6),
    .BUS0(_74161_2_pin3), .BUS1(_74161_2_pin4), .BUS2(_74161_2_pin5), .BUS3(_74161_2_pin6), .CLK(not_6_out),
    .Co(alu_slice_1_1_co), .AC0(_74541_2_pin9), .AC1(_74541_2_pin8), .AC2(_74541_2_pin7), .AC3(_74541_2_pin6));
  LED led_21 (.in(_74541_1_pin15));
  LED led_22 (.in(alu_slice_1_1_co));
  LED led_23 (.in(_74541_1_pin14));
  LED led_24 (.in(_74541_1_pin13));
  LED led_25 (.in(_74541_1_pin12));
  _74173 _74173_1 (
    .pin1(1'b0), .pin2(1'b0), .pin3(_74173_1_pin3), .pin4(_74138_1_pin1), .pin5(_74138_1_pin2),
    .pin6(_74138_1_pin3), .pin7(not_6_out), .pin8(1'b0), .pin9(1'b0), .pin10(1'b0), .pin11(_28c16_1_p20),
    .pin12(_28c16_1_p21), .pin13(_28c16_1_p22), .pin14(_74173_1_pin14), .pin15(1'b0), .pin16(1'b1));
  _74173 _74173_2 (
    .pin1(1'b0), .pin2(1'b0), .pin3(_74173_2_pin3), .pin4(_74173_2_pin4), .pin5(_74173_2_pin5),
    .pin6(_74173_2_pin6), .pin7(not_6_out), .pin8(1'b0), .pin9(1'b0), .pin10(1'b0), .pin11(_74173_2_pin11),
    .pin12(_28c16_1_p11), .pin13(_28c16_1_p10), .pin14(_28c16_1_p9), .pin15(1'b0), .pin16(1'b1));
  LED led_26 (.in(_74161_2_pin6));
  LED led_27 (.in(_74161_2_pin5));
  LED led_28 (.in(_74541_1_pin11));
  LED led_29 (.in(_74541_2_pin6));
  LED led_30 (.in(_74541_2_pin7));
  LED led_31 (.in(_74161_2_pin4));
  LED led_32 (.in(_74161_2_pin3));
  LED led_33 (.in(_74138_1_pin3));
  LED led_34 (.in(_74541_2_pin8));
  LED led_35 (.in(_74541_2_pin9));
  LED led_36 (.in(_74138_1_pin2));
  LED led_37 (.in(_74138_1_pin1));
  LED led_38 (.in(_74173_1_pin3));
  LED led_39 (.in(_74173_2_pin6));
  LED led_40 (.in(_74173_2_pin5));
  not not_7 (_74161_1_pin1, _74153_1_pin1);
  LED led_41 (.in(_74173_2_pin4));
  LED led_42 (.in(_74173_2_pin3));
  LED led_43 (.in(_74161_2_pin6));
  LED led_44 (.in(_74161_2_pin5));
  _74541 _74541_3 (
    .pin1(_74541_3_pin1), .pin2(_74173_2_pin3), .pin3(_74173_2_pin4), .pin4(_74173_2_pin5),
    .pin5(_74173_2_pin6), .pin6(1'b0), .pin7(1'b0), .pin8(1'b0), .pin9(1'b0), .pin10(1'b0),
    .pin15(_74161_2_pin6), .pin16(_74161_2_pin5), .pin17(_74161_2_pin4), .pin18(_74161_2_pin3),
    .pin19(_74541_3_pin1), .pin20(1'b1));  // open: pin11, pin12, pin13, pin14
  LED led_45 (.in(_74161_2_pin4));
  LED led_46 (.in(_74161_2_pin3));
  or or_1 (or_1_out, CLK1, _74138_1_pin9);
  not not_8 (not_8_out, or_1_out);
  LED led_47 (.in(not_8_out));
  LED led_48 (.in(_74173_2_pin6));
  LED led_49 (.in(_74153_1_pin1));
  LED led_50 (.in(_74173_2_pin5));
  LED led_51 (.in(_74173_2_pin4));
  _74153 _74153_1 (
    .pin1(_74153_1_pin1), .pin2(alu_slice_1_1_co), .pin3(1'b0), .pin4(_74138_1_pin2), .pin5(_74138_1_pin1),
    .pin6(_74173_1_pin3), .pin8(1'b0), .pin10(1'b1), .pin11(1'b1), .pin12(1'b1), .pin13(1'b1), .pin14(1'b0),
    .pin15(1'b1), .pin16(1'b1));  // open: pin7, pin9
  _7425 _7425_1 (
    .pin1(_74173_2_pin3), .pin2(_74173_2_pin4), .pin4(_74173_2_pin5), .pin5(_74173_2_pin6),
    .pin6(_74153_1_pin1), .pin7(1'b0), .pin8(_7425_1_pin8), .pin9(_74173_1_pin3), .pin10(_74138_1_pin1),
    .pin12(_74138_1_pin2), .pin13(_74138_1_pin3), .pin14(1'b1));  // open: pin3, pin11
  _7420 PC_DETECT (
    .pin1(_74173_2_pin6), .pin2(_74173_2_pin5), .pin4(_74173_2_pin4), .pin5(_74173_2_pin3),
    .pin6(_74541_1_pin1), .pin7(1'b0), .pin9(1'b1), .pin10(1'b1), .pin12(1'b1), .pin13(1'b1), .pin14(1'b1));  // open: pin3, pin8, pin11
  LED led_52 (.in(_74173_2_pin3));
  LED led_53 (.in(1'b0));
  LED led_54 (.in(_74161_2_pin6));
  LED led_55 (.in(_7425_1_pin8));
  not not_9 (_74541_3_pin1, _7425_1_pin8);
  LED led_56 (.in(_74161_2_pin5));
  LED led_57 (.in(_74161_2_pin4));
  LED led_58 (.in(_74161_2_pin3));
  _74219 _74219_1 (
    .A0(_74173_2_pin3), .A1(_74173_2_pin4), .A2(_74173_2_pin5), .A3(_74173_2_pin6), .D0(_74161_2_pin3),
    .D1(_74161_2_pin4), .D2(_74161_2_pin5), .D3(_74161_2_pin6), .Q0(_74161_2_pin3), .Q1(_74161_2_pin4),
    .Q2(_74161_2_pin5), .Q3(_74161_2_pin6), .nCS(_7425_1_pin8), .nWE(or_1_out), .VCC(1'b1), .GND(1'b0));
  not not_10 (not_10_out, or_1_out);
  _74244 _74244_1 (
    .pin1(not_10_out), .pin2(_74161_2_pin3), .pin4(_74161_2_pin4), .pin6(_74161_2_pin5),
    .pin8(_74161_2_pin6), .pin10(1'b0), .pin11(1'b1), .pin12(_74244_1_pin12), .pin13(1'b1),
    .pin14(_74244_1_pin14), .pin15(1'b1), .pin16(_74244_1_pin16), .pin17(1'b1), .pin18(_74244_1_pin18),
    .pin19(_7425_1_pin8), .pin20(1'b1));  // open: pin3, pin5, pin7, pin9
  LED led_59 (.in(_74244_1_pin12));
  LED led_60 (.in(_74244_1_pin14));
  LED led_61 (.in(_74244_1_pin16));
  LED led_62 (.in(_74244_1_pin18));

  // Notes on the sheet:
  //   ADD  1100
  //   SUB  0011 plus Cin
  //   AND  1000 plus AL
  //   OR      1110 plus AL
  //   XOR   0110 plus AL
  //   0000 = 0x0 // Q=0x00  
  //   1111 = 0xf // Q=0xff  
  //   1010 = 0xa // Q=A     
  //   1100 = 0xc // Q=B     
  //   0101 = 0x5 // Q=/A    
  //   0011 = 0x3 // Q=/B    
  //   1110 = 0xe // Q= A| B 
  //   1101 = 0xd // Q=/A| B 
  //   1011 = 0xb // Q= A|/B 
  //   0111 = 0x7 // Q=/A|/B 
  //   1000 = 0x8 // Q= A& B 
  //   0100 = 0x4 // Q=/A& B 
  //   0010 = 0x2 // Q= A&/B 
  //   0001 = 0x1 // Q=/A&/B 
  //   0110 = 0x6 // Q=  A XOR B 
  //   1001 = 0x9 // Q=/(A XOR B)
  //   OPCODE
  //   INSTRUCTION
  //   DECODER
  //   AL
  //   AR3
  //   AR2
  //   AR1
  //   AR0/Cin
  //   PROGRAM
  //   COUNTER
  //   ROM ADDRESS
  //   /PCL
  //   INSTRUCTION ROM
  //   BUS ACCESS
  //   /AE
  //   INSTRUCTION
  //   REGISTER
  //   Cout
  //   ALU RESULT BUS
  //   3
  //   2
  //   1
  //   0
  //   /RESET
  //   DATA BUS
  //   REGISTER
  //   Write
  //   Jump
  //   JUMP/ZERO 
  //   DETECTOR
  //   AC7
  //   REGISTER INPUT BUS
  //   FROM REGISTERS
endmodule
