// Digital circuit Alu_8bit.dig as structural Verilog
module Alu_8bit (
  input  BUS3,
  input  BUS2,
  input  BUS1,
  input  BUS0,
  input  BUS7,
  input  BUS6,
  input  BUS5,
  input  BUS4,
  input  CLK1,
  input  RES,
  input  OL,
  input  IX,
  input  XL,
  input  PL,
  input  in_27,
  input  in_28,
  input  UP_DN,
  input  CLK,
  input  IR5,
  input  IR6,
  input  IR7,
  output B0,
  output A0,
  output B1,
  output A1,
  output A2,
  output B2,
  output B3,
  output A3,
  output ALU3,
  output ALU2,
  output ALU1,
  output ALU0,
  output B4,
  output A4,
  output B5,
  output A5,
  output A6,
  output B6,
  output B7,
  output A7,
  output Cout
);

  wire _74138_1_pin7, _74138_1_pin9, _74138_1_pin10, _74138_1_pin11, _74138_1_pin12, _74138_1_pin13,
       _74138_1_pin14, _74138_1_pin15, _74153_1_pin14, _74153_2_pin14, _74153_3_pin14, _74153_4_pin14,
       _74153_5_pin14, _74153_6_pin14, _74153_7_pin14, _74153_8_pin14, _74161_1_pin11, _74161_1_pin12,
       _74161_1_pin13, _74161_1_pin14, _74161_2_pin11, _74161_2_pin12, _74161_2_pin13, _74161_2_pin14,
       _74173_3_pin3, _74173_3_pin4, _74173_3_pin5, _74173_3_pin6, _74189_1_pin5, _74189_1_pin7,
       _74189_1_pin9, _74189_1_pin11, _74191_1_pin1, _74191_1_pin2, _74191_1_pin3, _74191_1_pin6,
       _74191_1_pin9, _74191_1_pin10, _74191_1_pin15, _74283_1_pin9, _74283_2_pin1, _74283_2_pin4,
       _74283_2_pin10, _74283_2_pin13, diodebackward_1_out, diodebackward_2_out, diodebackward_7_out,
       diodebackward_12_out, diodebackward_16_out, dipswitch_1_out, dipswitch_2_out, dipswitch_3_out,
       dipswitch_4_out, not_1_out, not_2_out, not_3_out, not_4_out, not_5_out, not_6_out;

  _74138 _74138_1 (
    .pin1(IR5), .pin2(IR6), .pin3(IR7), .pin4(1'b0), .pin5(1'b0), .pin6(1'b1), .pin7(_74138_1_pin7),
    .pin8(1'b0), .pin9(_74138_1_pin9), .pin10(_74138_1_pin10), .pin11(_74138_1_pin11),
    .pin12(_74138_1_pin12), .pin13(_74138_1_pin13), .pin14(_74138_1_pin14), .pin15(_74138_1_pin15),
    .pin16(1'b1));
  DiodeBackward diodebackward_1 (.in(IR7), .out(diodebackward_1_out));
  PullUp pullup_1 (.out(diodebackward_1_out));
  DiodeBackward diodebackward_2 (.in(_74138_1_pin15), .out(diodebackward_2_out));
  DiodeBackward diodebackward_3 (.in(_74138_1_pin14), .out(diodebackward_2_out));
  DiodeBackward diodebackward_4 (.in(_74138_1_pin13), .out(diodebackward_2_out));
  DiodeBackward diodebackward_5 (.in(_74138_1_pin11), .out(diodebackward_2_out));
  DiodeBackward diodebackward_6 (.in(_74138_1_pin7), .out(diodebackward_2_out));
  not not_1 (not_1_out, diodebackward_1_out);
  LED led_1 (.in(not_1_out));
  PullUp pullup_2 (.out(diodebackward_2_out));
  DiodeBackward diodebackward_7 (.in(_74138_1_pin15), .out(diodebackward_7_out));
  DiodeBackward diodebackward_8 (.in(_74138_1_pin13), .out(diodebackward_7_out));
  DiodeBackward diodebackward_9 (.in(_74138_1_pin12), .out(diodebackward_7_out));
  DiodeBackward diodebackward_10 (.in(_74138_1_pin11), .out(diodebackward_7_out));
  DiodeBackward diodebackward_11 (.in(_74138_1_pin7), .out(diodebackward_7_out));
  not not_2 (not_2_out, diodebackward_2_out);
  LED led_2 (.in(not_2_out));
  PullUp pullup_3 (.out(diodebackward_7_out));
  DiodeBackward diodebackward_12 (.in(_74138_1_pin13), .out(diodebackward_12_out));
  DiodeBackward diodebackward_13 (.in(_74138_1_pin12), .out(diodebackward_12_out));
  DiodeBackward diodebackward_14 (.in(_74138_1_pin10), .out(diodebackward_12_out));
  DiodeBackward diodebackward_15 (.in(_74138_1_pin7), .out(diodebackward_12_out));
  not not_3 (not_3_out, diodebackward_7_out);
  LED led_3 (.in(not_3_out));
  PullUp pullup_4 (.out(diodebackward_12_out));
  DiodeBackward diodebackward_16 (.in(_74138_1_pin10), .out(diodebackward_16_out));
  not not_4 (not_4_out, diodebackward_12_out);
  LED led_4 (.in(not_4_out));
  PullUp pullup_5 (.out(diodebackward_16_out));
  not not_5 (not_5_out, diodebackward_16_out);
  LED led_5 (.in(not_5_out));
  _74161 _74161_1 (
    .pin1(RES), .pin2(CLK1), .pin3(BUS0), .pin4(BUS1), .pin5(BUS2), .pin6(BUS3), .pin7(1'b1), .pin8(1'b0),
    .pin9(PL), .pin10(1'b1), .pin11(_74161_1_pin11), .pin12(_74161_1_pin12), .pin13(_74161_1_pin13),
    .pin14(_74161_1_pin14), .pin16(1'b1));  // open: pin15
  _74153 _74153_1 (
    .pin1(1'b0), .pin2(BUS3), .pin3(not_2_out), .pin4(not_3_out), .pin5(not_4_out), .pin6(not_5_out),
    .pin7(A3), .pin8(1'b0), .pin9(B3), .pin10(1'b0), .pin11(1'b1), .pin12(1'b0), .pin13(1'b1),
    .pin14(_74153_1_pin14), .pin15(not_1_out), .pin16(1'b1));
  _74153 _74153_2 (
    .pin1(1'b0), .pin2(BUS2), .pin3(not_2_out), .pin4(not_3_out), .pin5(not_4_out), .pin6(not_5_out),
    .pin7(A2), .pin8(1'b0), .pin9(B2), .pin10(1'b0), .pin11(1'b1), .pin12(1'b0), .pin13(1'b1),
    .pin14(_74153_2_pin14), .pin15(not_1_out), .pin16(1'b1));
  _74153 _74153_3 (
    .pin1(1'b0), .pin2(BUS1), .pin3(not_2_out), .pin4(not_3_out), .pin5(not_4_out), .pin6(not_5_out),
    .pin7(A1), .pin8(1'b0), .pin9(B1), .pin10(1'b0), .pin11(1'b1), .pin12(1'b0), .pin13(1'b1),
    .pin14(_74153_3_pin14), .pin15(not_1_out), .pin16(1'b1));
  _74153 _74153_4 (
    .pin1(1'b0), .pin2(BUS0), .pin3(not_2_out), .pin4(not_3_out), .pin5(not_4_out), .pin6(not_5_out),
    .pin7(A0), .pin8(1'b0), .pin9(B0), .pin10(1'b0), .pin11(1'b1), .pin12(1'b0), .pin13(1'b1),
    .pin14(_74153_4_pin14), .pin15(not_1_out), .pin16(1'b1));
  _74153 _74153_5 (
    .pin1(1'b0), .pin2(BUS4), .pin3(not_2_out), .pin4(not_3_out), .pin5(not_4_out), .pin6(not_5_out),
    .pin7(A7), .pin8(1'b0), .pin9(B7), .pin10(1'b0), .pin11(1'b1), .pin12(1'b0), .pin13(1'b1),
    .pin14(_74153_5_pin14), .pin15(not_1_out), .pin16(1'b1));
  _74153 _74153_6 (
    .pin1(1'b0), .pin2(BUS5), .pin3(not_2_out), .pin4(not_3_out), .pin5(not_4_out), .pin6(not_5_out),
    .pin7(A6), .pin8(1'b0), .pin9(B6), .pin10(1'b0), .pin11(1'b1), .pin12(1'b0), .pin13(1'b1),
    .pin14(_74153_6_pin14), .pin15(not_1_out), .pin16(1'b1));
  _74153 _74153_7 (
    .pin1(1'b0), .pin2(BUS6), .pin3(not_2_out), .pin4(not_3_out), .pin5(not_4_out), .pin6(not_5_out),
    .pin7(A5), .pin8(1'b0), .pin9(B5), .pin10(1'b0), .pin11(1'b1), .pin12(1'b0), .pin13(1'b1),
    .pin14(_74153_7_pin14), .pin15(not_1_out), .pin16(1'b1));
  _74153 _74153_8 (
    .pin1(1'b0), .pin2(BUS7), .pin3(not_2_out), .pin4(not_3_out), .pin5(not_4_out), .pin6(not_5_out),
    .pin7(A4), .pin8(1'b0), .pin9(B4), .pin10(1'b0), .pin11(1'b1), .pin12(1'b0), .pin13(1'b1),
    .pin14(_74153_8_pin14), .pin15(not_1_out), .pin16(1'b1));
  LED led_6 (.in(_74161_1_pin11));
  LED led_7 (.in(_74161_1_pin12));
  not not_6 (not_6_out, _74138_1_pin9);
  LED led_8 (.in(_74161_1_pin13));
  LED led_9 (.in(_74161_1_pin14));
  LED led_10 (.in(not_6_out));
  _74283 _74283_1 (
    .pin1(ALU1), .pin2(B1), .pin3(A1), .pin4(ALU0), .pin5(A0), .pin6(B0), .pin7(not_5_out), .pin8(1'b0),
    .pin9(_74283_1_pin9), .pin10(ALU3), .pin11(B3), .pin12(A3), .pin13(ALU2), .pin14(A2), .pin15(B2),
    .pin16(1'b1));
  _74283 _74283_2 (
    .pin1(_74283_2_pin1), .pin2(B5), .pin3(A5), .pin4(_74283_2_pin4), .pin5(A4), .pin6(B4),
    .pin7(_74283_1_pin9), .pin8(1'b0), .pin9(Cout), .pin10(_74283_2_pin10), .pin11(B7), .pin12(A7),
    .pin13(_74283_2_pin13), .pin14(A6), .pin15(B6), .pin16(1'b1));
  LED led_11 (.in(1'b0));
  LED led_12 (.in(_74191_1_pin6));
  LED led_13 (.in(_74191_1_pin2));
  DipSwitch dipswitch_1 (.out(dipswitch_1_out));
  DipSwitch dipswitch_2 (.out(dipswitch_2_out));
  DipSwitch dipswitch_3 (.out(dipswitch_3_out));
  DipSwitch dipswitch_4 (.out(dipswitch_4_out));
  LED led_14 (.in(_74191_1_pin3));
  _74191 _74191_1 (
    .pin1(_74191_1_pin1), .pin2(_74191_1_pin2), .pin3(_74191_1_pin3), .pin4(1'b0), .pin5(UP_DN),
    .pin6(_74191_1_pin6), .pin7(1'b0), .pin8(1'b0), .pin9(_74191_1_pin9), .pin10(_74191_1_pin10),
    .pin11(1'b1), .pin14(CLK), .pin15(_74191_1_pin15), .pin16(1'b1));  // open: pin12, pin13
  _74189 _74189_1 (
    .pin1(_74191_1_pin3), .pin2(in_27), .pin3(in_28), .pin4(dipswitch_1_out), .pin5(_74189_1_pin5),
    .pin6(dipswitch_2_out), .pin7(_74189_1_pin7), .pin8(1'b0), .pin9(_74189_1_pin9), .pin10(dipswitch_3_out),
    .pin11(_74189_1_pin11), .pin12(dipswitch_4_out), .pin13(1'b0), .pin14(_74191_1_pin6),
    .pin15(_74191_1_pin2), .pin16(1'b1));
  LED led_15 (.in(Cout));
  LED led_16 (.in(_74283_2_pin10));
  LED led_17 (.in(_74283_2_pin13));
  LED led_18 (.in(_74283_2_pin1));
  _74173 _74173_1 (
    .pin1(1'b0), .pin2(1'b0), .pin3(_74153_8_pin14), .pin4(_74153_7_pin14), .pin5(_74153_6_pin14),
    .pin6(_74153_5_pin14), .pin7(CLK1), .pin8(1'b0), .pin9(1'b0), .pin10(1'b0), .pin11(_74283_2_pin10),
    .pin12(_74283_2_pin13), .pin13(_74283_2_pin1), .pin14(_74283_2_pin4), .pin15(RES), .pin16(1'b1));
  LED led_19 (.in(_74283_2_pin4));
  LED led_20 (.in(ALU3));
  LED led_21 (.in(ALU2));
  LED led_22 (.in(ALU1));
  LED led_23 (.in(_74189_1_pin11));
  LED led_24 (.in(_74189_1_pin9));
  LED led_25 (.in(_74189_1_pin7));
  LED led_26 (.in(_74189_1_pin5));
  LED led_27 (.in(ALU0));
  DipSwitch dipswitch_5 (.out(_74191_1_pin15));
  DipSwitch dipswitch_6 (.out(_74191_1_pin1));
  DipSwitch dipswitch_7 (.out(_74191_1_pin10));
  DipSwitch dipswitch_8 (.out(_74191_1_pin10));
  DipSwitch dipswitch_9 (.out(_74191_1_pin9));
  _74173 _74173_2 (
    .pin1(1'b0), .pin2(1'b0), .pin3(_74153_4_pin14), .pin4(_74153_3_pin14), .pin5(_74153_2_pin14),
    .pin6(_74153_1_pin14), .pin7(CLK1), .pin8(1'b0), .pin9(1'b0), .pin10(1'b0), .pin11(ALU3), .pin12(ALU2),
    .pin13(ALU1), .pin14(ALU0), .pin15(RES), .pin16(1'b1));
  _74173 _74173_3 (
    .pin1(1'b0), .pin2(1'b0), .pin3(_74173_3_pin3), .pin4(_74173_3_pin4), .pin5(_74173_3_pin5),
    .pin6(_74173_3_pin6), .pin7(CLK1), .pin8(1'b0), .pin9(OL), .pin10(OL), .pin11(ALU3), .pin12(ALU2),
    .pin13(ALU1), .pin14(ALU0), .pin15(1'b0), .pin16(1'b1));
  LED led_28 (.in(_74173_3_pin6));
  LED led_29 (.in(_74173_3_pin5));
  LED led_30 (.in(_74173_3_pin4));
  LED led_31 (.in(_74173_3_pin3));
  _74161 _74161_2 (
    .pin1(1'b1), .pin2(CLK1), .pin3(ALU0), .pin4(ALU1), .pin5(ALU2), .pin6(ALU3), .pin7(IX), .pin8(1'b0),
    .pin9(XL), .pin10(1'b1), .pin11(_74161_2_pin11), .pin12(_74161_2_pin12), .pin13(_74161_2_pin13),
    .pin14(_74161_2_pin14), .pin16(1'b1));  // open: pin15
  LED led_32 (.in(_74161_2_pin11));
  LED led_33 (.in(_74161_2_pin12));
  LED led_34 (.in(_74161_2_pin13));
  LED led_35 (.in(_74161_2_pin14));

  // Notes on the sheet:
  //   CLK1: Hz: 10
  //   ADD  1100
  //   SUB  0011 plus Cin
  //   AND  1000 plus AL
  //   OR      1110 plus AL
  //   XOR   0110 plus AL
  //   0000 = 0x0 // Q=0x00  
  //   1111 = 0xf // Q=0xff  
  //   1010 = 0xa // Q=A     
  //   1100 = 0xc // Q=B     
  //   0101 = 0x5 // Q=/A    
  //   0011 = 0x3 // Q=/B    
  //   1110 = 0xe // Q= A| B 
  //   1101 = 0xd // Q=/A| B 
  //   1011 = 0xb // Q= A|/B 
  //   0111 = 0x7 // Q=/A|/B 
  //   1000 = 0x8 // Q= A& B 
  //   0100 = 0x4 // Q=/A& B 
  //   0010 = 0x2 // Q= A&/B 
  //   0001 = 0x1 // Q=/A&/B 
  //   0110 = 0x6 // Q=  A XOR B 
  //   1001 = 0x9 // Q=/(A XOR B)
  //   INSTRUCTION
  //   DECODER
  //   AL
  //   AR3
  //   AR2
  //   AR1
  //   AR0/Cin
  //   PROGRAM
  //   COUNTER
  //   MUX3
  //   MUX2
  //   MUX1
  //   MUX0
  //   MUX7
  //   MUX6
  //   MUX5
  //   MUX4
  //   Write
  //   ADDER
  //   REGISTER
  //   Cout
  //   7
  //   6
  //   ALU RESULT BUS
  //   5
  //   4
  //   3
  //   2
  //   ACCUMULATOR
  //   1
  //   0
  //   OUTPUT REGISTER
  //   X REGISTER
endmodule
