// Digital circuit alu_acc1.dig as structural Verilog
module alu_acc1 (
  input  Cin,
  input  AL,
  input  AR3,
  input  AR2,
  input  AR1,
  input  AR0,
  input  BUS3,
  input  BUS2,
  input  BUS1,
  input  BUS0,
  input  AC3,
  input  AC2,
  input  AC1,
  input  AC0,
  input  CLK1,
  input  RES,
  output B0,
  output A0,
  output B1,
  output A1,
  output A2,
  output B2,
  output B3,
  output A3,
  output ALU3,
  output ALU2,
  output ALU1,
  output ALU0,
  output Cout
);

  wire _74153_1_pin14, _74153_2_pin14, _74153_3_pin14, _74153_4_pin14;

  _74153 _74153_1 (
    .pin1(1'b0), .pin2(BUS3), .pin3(AR3), .pin4(AR2), .pin5(AR1), .pin6(AR0), .pin7(A3), .pin8(1'b0),
    .pin9(B3), .pin10(1'b0), .pin11(1'b1), .pin12(1'b0), .pin13(1'b1), .pin14(_74153_1_pin14), .pin15(AL),
    .pin16(1'b1));
  _74153 _74153_2 (
    .pin1(1'b0), .pin2(BUS2), .pin3(AR3), .pin4(AR2), .pin5(AR1), .pin6(AR0), .pin7(A2), .pin8(1'b0),
    .pin9(B2), .pin10(1'b0), .pin11(1'b1), .pin12(1'b0), .pin13(1'b1), .pin14(_74153_2_pin14), .pin15(AL),
    .pin16(1'b1));
  _74153 _74153_3 (
    .pin1(1'b0), .pin2(BUS1), .pin3(AR3), .pin4(AR2), .pin5(AR1), .pin6(AR0), .pin7(A1), .pin8(1'b0),
    .pin9(B1), .pin10(1'b0), .pin11(1'b1), .pin12(1'b0), .pin13(1'b1), .pin14(_74153_3_pin14), .pin15(AL),
    .pin16(1'b1));
  _74153 _74153_4 (
    .pin1(1'b0), .pin2(BUS0), .pin3(AR3), .pin4(AR2), .pin5(AR1), .pin6(AR0), .pin7(A0), .pin8(1'b0),
    .pin9(B0), .pin10(1'b0), .pin11(1'b1), .pin12(1'b0), .pin13(1'b1), .pin14(_74153_4_pin14), .pin15(AL),
    .pin16(1'b1));
  _74283 _74283_1 (
    .pin1(ALU1), .pin2(B1), .pin3(A1), .pin4(ALU0), .pin5(A0), .pin6(B0), .pin7(Cin), .pin8(1'b0),
    .pin9(Cout), .pin10(ALU3), .pin11(B3), .pin12(A3), .pin13(ALU2), .pin14(A2), .pin15(B2), .pin16(1'b1));
  LED led_1 (.in(Cout));
  LED led_2 (.in(ALU3));
  LED led_3 (.in(ALU2));
  LED led_4 (.in(ALU1));
  LED led_5 (.in(ALU0));
  _74173 _74173_1 (
    .pin1(1'b0), .pin2(1'b0), .pin3(_74153_4_pin14), .pin4(_74153_3_pin14), .pin5(_74153_2_pin14),
    .pin6(_74153_1_pin14), .pin7(CLK1), .pin8(1'b0), .pin9(1'b0), .pin10(1'b0), .pin11(ALU3), .pin12(ALU2),
    .pin13(ALU1), .pin14(ALU0), .pin15(RES), .pin16(1'b1));

  // Notes on the sheet:
  //   ADD  1100
  //   SUB  0011 plus Cin
  //   AND  1000 plus AL
  //   OR      1110 plus AL
  //   XOR   0110 plus AL
  //   0000 = 0x0 // Q=0x00  
  //   1111 = 0xf // Q=0xff  
  //   1010 = 0xa // Q=A     
  //   1100 = 0xc // Q=B     
  //   0101 = 0x5 // Q=/A    
  //   0011 = 0x3 // Q=/B    
  //   1110 = 0xe // Q= A| B 
  //   1101 = 0xd // Q=/A| B 
  //   1011 = 0xb // Q= A|/B 
  //   0111 = 0x7 // Q=/A|/B 
  //   1000 = 0x8 // Q= A& B 
  //   0100 = 0x4 // Q=/A& B 
  //   0010 = 0x2 // Q= A&/B 
  //   0001 = 0x1 // Q=/A&/B 
  //   0110 = 0x6 // Q=  A XOR B 
  //   1001 = 0x9 // Q=/(A XOR B)
endmodule
