// Digital circuit alu_slice_1.dig as structural Verilog
module alu_slice_1 (
  input  Ci,
  input  AL,
  input  AR0,
  input  AR1,
  input  AR2,
  input  AR3,
  input  ALU0,
  input  ALU1,
  input  ALU2,
  input  ALU3,
  input  BUS0,
  input  BUS1,
  input  BUS2,
  input  BUS3,
  input  CLK,
  output Co,
  output AC0,
  output AC1,
  output AC2,
  output AC3
);

  wire _74153_1_p15, _74153_1_p16, _74153_2_p15, _74153_2_p16, _74153_3_p15, _74153_3_p16, _74153_4_p15,
       _74153_4_p16, _74283_1_p12, _74283_1_p13, _74283_1_p14, _74283_1_p15;

  // _74153 _74153_1: pin names not known; wires that end beside it: ALU3, BUS3, AL, 1'b0, 1'b1, 1'b0, 1'b1, 1'b0, AR0, AR1, AR2, AR3, 1'b1, 1'b0, _74153_1_p15, _74153_1_p16
  // _74153 _74153_2: pin names not known; wires that end beside it: ALU2, BUS2, AL, 1'b0, 1'b1, 1'b0, 1'b1, 1'b0, AR0, AR1, AR2, AR3, 1'b1, 1'b0, _74153_2_p15, _74153_2_p16
  // _74153 _74153_3: pin names not known; wires that end beside it: ALU1, BUS1, AL, 1'b0, 1'b1, 1'b0, 1'b1, 1'b0, AR0, AR1, AR2, AR3, 1'b1, 1'b0, _74153_3_p15, _74153_3_p16
  // _74153 _74153_4: pin names not known; wires that end beside it: ALU0, BUS0, AL, 1'b0, 1'b1, 1'b0, 1'b1, 1'b0, AR0, AR1, AR2, AR3, 1'b1, 1'b0, _74153_4_p15, _74153_4_p16
  // _74283 _74283_1: pin names not known; wires that end beside it: Ci, _74153_4_p15, _74153_3_p15, _74153_2_p15, _74153_1_p15, _74153_4_p16, _74153_3_p16, _74153_2_p16, _74153_1_p16, 1'b1, 1'b0, _74283_1_p12, _74283_1_p13, _74283_1_p14, _74283_1_p15, Co
  LED led_1 (.in(_74283_1_p15));
  LED led_2 (.in(Co));
  LED led_3 (.in(_74283_1_p14));
  LED led_4 (.in(_74283_1_p13));
  LED led_5 (.in(_74283_1_p12));
  // _74173 _74173_1: pin names not known; wires that end beside it: _74283_1_p12, 1'b1, 1'b0, 1'b0, _74283_1_p13, _74283_1_p14, _74283_1_p15, CLK, 1'b0, 1'b0, 1'b0, 1'b0, AC0, AC1, AC2, AC3
endmodule
