// Digital circuit suite_16_test_1.dig as structural Verilog
module suite_16_test_1 (
  input  in_1,
  input  in_2,
  input  in_3,
  input  in_4,
  input  in_5,
  input  in_6,
  input  in_7,
  input  in_8,
  input  in_9,
  input  in_10,
  input  in_11,
  input  in_12,
  input  in_13,
  input  in_14,
  input  in_15,
  input  in_16,
  input  in_17,
  input  in_18,
  input  in_19,
  input  in_20,
  input  in_21,
  input  in_22,
  input  in_23,
  input  in_24,
  input  in_25,
  input  in_26,
  input  in_27,
  input  in_28,
  input  in_29,
  input  in_30,
  input  in_31,
  input  in_32,
  input  AR3,
  input  AR2,
  input  AR1,
  input  AR0,
  input  AL,
  input  in_38
);

  wire _16_bit_alu_1_c15, _16_bit_alu_1_q0, _16_bit_alu_1_q1, _16_bit_alu_1_q2, _16_bit_alu_1_q3,
       _16_bit_alu_1_q4, _16_bit_alu_1_q5, _16_bit_alu_1_q6, _16_bit_alu_1_q7, _16_bit_alu_1_q8,
       _16_bit_alu_1_q9, _16_bit_alu_1_q10, _16_bit_alu_1_q11, _16_bit_alu_1_q12, _16_bit_alu_1_q13,
       _16_bit_alu_1_q14, _16_bit_alu_1_q15;

  LED led_1 (.in(in_1));
  LED led_2 (.in(in_2));
  LED led_3 (.in(in_17));
  LED led_4 (.in(in_3));
  LED led_5 (.in(in_4));
  LED led_6 (.in(in_18));
  LED led_7 (.in(in_19));
  LED led_8 (.in(in_5));
  LED led_9 (.in(in_6));
  LED led_10 (.in(in_20));
  LED led_11 (.in(in_21));
  LED led_12 (.in(in_7));
  LED led_13 (.in(in_8));
  LED led_14 (.in(in_22));
  LED led_15 (.in(in_23));
  LED led_16 (.in(in_9));
  LED led_17 (.in(in_10));
  LED led_18 (.in(in_24));
  LED led_19 (.in(in_25));
  LED led_20 (.in(in_11));
  LED led_21 (.in(in_12));
  LED led_22 (.in(in_26));
  LED led_23 (.in(in_27));
  LED led_24 (.in(in_13));
  LED led_25 (.in(in_14));
  LED led_26 (.in(in_28));
  LED led_27 (.in(in_29));
  LED led_28 (.in(in_15));
  LED led_29 (.in(in_16));
  LED led_30 (.in(in_30));
  LED led_31 (.in(in_31));
  LED led_32 (.in(in_32));
  _16_bit_alu _16_bit_alu_1 (
    .AR3(AR3), .AR2(AR2), .AR1(AR1), .AR0(AR0), .AL(AL), .A15(in_17), .A14(in_18), .A13(in_19), .A12(in_20),
    .A11(in_21), .A10(in_22), .A9(in_23), .A8(in_24), .A7(in_25), .A6(in_26), .A5(in_27), .A4(in_28),
    .A3(in_29), .A2(in_30), .A1(in_31), .A0(in_32), .B15(in_1), .B14(in_2), .B13(in_3), .B12(in_4),
    .B11(in_5), .B10(in_6), .B9(in_7), .B8(in_8), .B7(in_9), .B6(in_10), .B5(in_11), .B4(in_12), .B3(in_13),
    .B2(in_14), .B1(in_15), .B0(in_16), .CLK(in_38), .Q15(_16_bit_alu_1_q15), .Q14(_16_bit_alu_1_q14),
    .Q13(_16_bit_alu_1_q13), .Q12(_16_bit_alu_1_q12), .Q11(_16_bit_alu_1_q11), .Q10(_16_bit_alu_1_q10),
    .Q9(_16_bit_alu_1_q9), .Q8(_16_bit_alu_1_q8), .Q7(_16_bit_alu_1_q7), .Q6(_16_bit_alu_1_q6),
    .Q5(_16_bit_alu_1_q5), .Q4(_16_bit_alu_1_q4), .Q3(_16_bit_alu_1_q3), .Q2(_16_bit_alu_1_q2),
    .Q1(_16_bit_alu_1_q1), .Q0(_16_bit_alu_1_q0), .C15(_16_bit_alu_1_c15));
  LED led_33 (.in(_16_bit_alu_1_q15));
  LED led_34 (.in(_16_bit_alu_1_c15));
  LED led_35 (.in(_16_bit_alu_1_q14));
  LED led_36 (.in(_16_bit_alu_1_q13));
  LED led_37 (.in(_16_bit_alu_1_q12));
  LED led_38 (.in(_16_bit_alu_1_q11));
  LED led_39 (.in(_16_bit_alu_1_q10));
  LED led_40 (.in(_16_bit_alu_1_q9));
  LED led_41 (.in(_16_bit_alu_1_q8));
  LED led_42 (.in(_16_bit_alu_1_q7));
  LED led_43 (.in(_16_bit_alu_1_q6));
  LED led_44 (.in(_16_bit_alu_1_q5));
  LED led_45 (.in(_16_bit_alu_1_q4));
  LED led_46 (.in(_16_bit_alu_1_q3));
  LED led_47 (.in(_16_bit_alu_1_q2));
  LED led_48 (.in(_16_bit_alu_1_q1));
  LED led_49 (.in(_16_bit_alu_1_q0));

  // Notes on the sheet:
  //   LD      1100
  //   AND   1000
  //   OR      1110
  //   XOR    0110
  //   ADD    1100
  //   SUB    0011
  //   ST
  //   BCC    1110
endmodule
